# Fritzing sketch Circuit Diagram (saved by Fritzing 0.9.3b)

parts:
  U1 = LIPO-1000mAh [package=lipo-1000]
  A1 = Teensy 4.0
  U2 = Mini-360 DC-DC Buck converter [package=THT]
  A2 = WMYCONGCONG buck converter
  A3 = Raspberry Pi 5
  A4 = cks pd65W
  J1 = Basic Servo
  Part1 = Adafruit BNO055 STEMMA QT [part_number="Adafruit #4646"]
  DC_Mot_Enc1 = DC Motor with two-phase hall-encoder [part_number=VT-E-G25A-06-177E]

nets:
  N1: U1.+, U2.IN+, A2.Pin_2, A4.Pin_1
  GND: U1.-, A1.pin_1, A1.pin_17, A1.pin_32, U2.IN-, A2.Pin_3, A3.GND, A4.Pin_2, Part1.GND
  N2: A1.pin_2, DC_Mot_Enc1.pin4
  N3: A1.pin_3, DC_Mot_Enc1.pin5
  N4: A1.pin_5, J1.pulse
  N5: A1.pin_9, A3.GPIO15
  N6: A1.pin_10, A3.GPIO14
  N7: A1.pin_16, A1.pin_31, Part1.3.3V, DC_Mot_Enc1.pin1
  N8: A1.pin_25, Part1.SDA
  N9: A1.pin_26, Part1.SCL
  N10: A1.pin33, A2.Pin_4
  N11: U2.OUT+, J1.vcc
  N12: U2.OUT-, J1.gnd

custom parts:
  Teensy 4.0: The Teensy is a complete USB-based microcontoller development system, in a very small footprint, capable of implementing many types of projects. All programming is done via the USB port. No special programmer is needed, only a standard micro-USB cable and a PC or Macintosh with a USB port. (Oct 2023 added the VBUS pad at user request.)
  Mini-360 DC-DC Buck converter: Mini-360 DC-DC Buck converter. Tiny buck step down voltage converter, input voltage 4.75 to 23V output 1 to 17V adjustable. Available from ebay and the like.
  WMYCONGCONG buck converter: These amazing little DC-DC converters feature a wide input voltage of 4.5-24V and the output voltage can be set to one of six fixed voltages, or fully variable, just by bridging the relevant solder pads on the back of the PCB..
  Raspberry Pi 5: The RPi5, a faster version of the awesome Raspberry Pi4B ARM Board with 40 pin gpio.
  cks pd65W: QC4.0 QC3.0 Type-C USB PD65W Fast Charging Adapter Module DC8-32V 3.25A 65W Step Down Module For Huawei SCP/FCP Apple PD.
  Adafruit BNO055 STEMMA QT: If you've ever ordered and wire up a 9-DOF sensor, chances are you've also realized the challenge of turning the sensor data from an accelerometer, gyroscope, and magnetometer into actual "3D space orientation"! Orientation is a hard problem to solve. The sensor fusion algorithms (the secret sauce that blends accelerometer, magnetometer, and gyroscope data into stable three-axis orientation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
